// Digital circuit lab2_part2.dig as structural Verilog
module lab2_part2 (
  input  in0,
  input  in1,
  input  in2,
  input  in3,
  output seg_a,
  output seg_f,
  output seg_b,
  output seg_g,
  output seg_e,
  output seg_c,
  output seg_d,
  output seg_dp,
  output sign_a,
  output sign_f,
  output sign_b,
  output sign_g,
  output sign_e,
  output sign_c,
  output sign_d,
  output sign_dp
);

  wire and_1_out, and_2_out, and_3_out, and_4_out, and_5_out, and_6_out, and_7_out, and_8_out, and_9_out,
       demultiplexer_1_out_0, demultiplexer_1_out_1, demultiplexer_1_out_2, demultiplexer_1_out_3,
       demultiplexer_1_out_4, demultiplexer_1_out_5, demultiplexer_1_out_6, demultiplexer_1_out_7, or_1_out,
       or_3_out, or_5_out, or_10_out, or_13_out, or_14_out, or_15_out, val0, val1, val2, val3, xor_1_out,
       xor_2_out, xor_3_out, xor_4_out;
  wire [3:0] multiplexer_1_out, out0;

  Demultiplexer #(.Selector_Bits(3)) demultiplexer_1 (
    .sel(multiplexer_1_out[2:0]), .in(1'b1), .out_0(demultiplexer_1_out_0), .out_1(demultiplexer_1_out_1),
    .out_2(demultiplexer_1_out_2), .out_3(demultiplexer_1_out_3), .out_4(demultiplexer_1_out_4),
    .out_5(demultiplexer_1_out_5), .out_6(demultiplexer_1_out_6), .out_7(demultiplexer_1_out_7));
  assign {val3, val2, val1, val0} = ~{in3, in2, in1, in0};  // Not not_1, 4 bits wide
  Multiplexer #(.Bits(4)) multiplexer_1 (.sel(in3), .in_0({in3, in2, in1, in0}), .in_1(out0), .out(multiplexer_1_out));
  or or_1 (or_1_out, demultiplexer_1_out_0, demultiplexer_1_out_7);
  or or_2 (seg_a, demultiplexer_1_out_7, demultiplexer_1_out_5, demultiplexer_1_out_3, demultiplexer_1_out_2, or_1_out);
  or or_3 (or_3_out, demultiplexer_1_out_2, demultiplexer_1_out_0);
  Seven_Seg seven_seg_1 (.a(1'b0), .b(1'b0), .c(1'b0), .d(1'b0), .e(1'b0), .f(1'b0), .g(in3), .dp(1'b0));
  or or_4 (seg_b, demultiplexer_1_out_4, demultiplexer_1_out_7, demultiplexer_1_out_1, demultiplexer_1_out_3, or_3_out);
  or or_5 (or_5_out, demultiplexer_1_out_3, demultiplexer_1_out_1, demultiplexer_1_out_0);
  or or_6 (seg_c, demultiplexer_1_out_6, demultiplexer_1_out_5, demultiplexer_1_out_7, demultiplexer_1_out_4, or_5_out);
  Seven_Seg seven_seg_2 (.a(seg_a), .b(seg_b), .c(seg_c), .d(seg_d), .e(seg_e), .f(seg_f), .g(seg_g), .dp(1'b0));
  or or_7 (seg_d, demultiplexer_1_out_5, demultiplexer_1_out_3, demultiplexer_1_out_6, demultiplexer_1_out_2, demultiplexer_1_out_0);
  or or_8 (seg_e, demultiplexer_1_out_6, demultiplexer_1_out_2, demultiplexer_1_out_0);
  or or_9 (seg_f, demultiplexer_1_out_6, demultiplexer_1_out_5, demultiplexer_1_out_4, demultiplexer_1_out_0);
  and and_1 (and_1_out, in3, demultiplexer_1_out_0);
  or or_10 (or_10_out, demultiplexer_1_out_2, and_1_out);
  or or_11 (seg_g, or_10_out, demultiplexer_1_out_3, demultiplexer_1_out_4, demultiplexer_1_out_5, demultiplexer_1_out_6);
  xor xor_1 (xor_1_out, val0, 1'b1);
  and and_2 (and_2_out, 1'b1, val0);
  xor xor_2 (xor_2_out, val1, 1'b0);
  and and_3 (and_3_out, 1'b0, val1);
  xor xor_3 (xor_3_out, val2, 1'b0);
  and and_4 (and_4_out, 1'b0, val2);
  xor xor_4 (xor_4_out, val3, 1'b0);
  and and_5 (and_5_out, 1'b0, val3);
  and and_6 (and_6_out, 1'b0, xor_1_out);
  and and_7 (and_7_out, or_13_out, xor_2_out);
  and and_8 (and_8_out, or_14_out, xor_3_out);
  and and_9 (and_9_out, or_15_out, xor_4_out);
  xor xor_5 (out0[3], xor_4_out, or_15_out);
  // Or or_12 has open pins: In_1=and_9_out, In_2=and_5_out, out=open
  xor xor_6 (out0[0], xor_1_out, 1'b0);
  or or_13 (or_13_out, and_6_out, and_2_out);
  xor xor_7 (out0[1], xor_2_out, or_13_out);
  or or_14 (or_14_out, and_7_out, and_3_out);
  xor xor_8 (out0[2], xor_3_out, or_14_out);
  or or_15 (or_15_out, and_8_out, and_4_out);

  assign seg_dp = 1'b0;
  assign sign_a = 1'b0;
  assign sign_b = 1'b0;
  assign sign_c = 1'b0;
  assign sign_d = 1'b0;
  assign sign_dp = 1'b0;
  assign sign_e = 1'b0;
  assign sign_f = 1'b0;
  assign sign_g = in3;

  // Notes on the sheet:
  //   Interface (do not edit the content inside this box)
  //   Outputs:
  //   Inputs
  //   Sign
  //   Decimal Number
endmodule

/* Test case:
in3 in2 in1 in0  sign_a sign_b sign_c sign_d sign_e sign_f sign_g  seg_a seg_b seg_c seg_d seg_e seg_f seg_g
 0   0   0   0    0      0      0      0      0      0      0       1     1     1     1     1     1     0
*/
